# Fritzing sketch nodeMCU_HC-SR501 (saved by Fritzing 0.9.3b)
breadboards: 1

parts:
  Part1 = HC-SR501 Body Sensor Module [part_number=HC-SR501]
  U1 = NodeMCU V1.0

nets:
  VCC: Part1.VCC, U1.Vin
  N1: Part1.OUT, U1.D3
  GND: Part1.GND, U1.GND

custom parts:
  HC-SR501 Body Sensor Module: HC-SR501 Pyroelectric Infrared PIR Motion Sensor Detector Module
  NodeMCU V1.0: ESP8266 based NodeMCU
